# Fritzing sketch MainSCH (saved by Fritzing 1.0.3b)
breadboards: 1

parts:
  Controller = Arduino Uno (Rev3)
  Temperature_Sensor = TMP36 [package=to-92]
  R1 = Resistor [tolerance=±5% power=0.25W resistance=470 package=THT]
  Part1 = Soil Moisture Sensor

nets:
  N1: Controller.A0, Part1.SIG
  GND: Controller.GND, Temperature_Sensor.GND, Part1.GND
  N2: Controller.D4, R1.Pin_1
  5V: Controller.VIN, Temperature_Sensor.VCC, Part1.VCC
  N3: Temperature_Sensor.VOUT, R1.Pin_0
